// Logisim project Subtracter.circ as structural Verilog: 3 circuits, main circuit main
module main (
  input  [3:0] A,
  input  [3:0] B
);
endmodule

module Full_Subtracter (
  input  borrow_in,
  input  bit_1,
  input  bit_0,
  output borrow_out,
  output diff
);
endmodule

module Half_Subtracter (
  input  bit_1,
  input  bit_0,
  output borrow,
  output diff
);

  wire not_1_out;

  not not_1 (not_1_out, bit_1);
  and and_1 (borrow, not_1_out, bit_0);
  xor xor_1 (diff, bit_1, bit_0);
endmodule
