// Logisim project minirv.circ as structural Verilog: 1 circuit, main circuit main
module main (
);

  wire clock_1_out, clock_2_out, clock_3_out, comparator_1_eq, comparator_2_eq, comparator_3_eq,
       comparator_4_eq, comparator_5_eq, comparator_6_eq, comparator_7_eq, comparator_9_eq, comparator_10_eq,
       comparator_11_eq, comparator_12_eq, comparator_13_eq, comparator_14_eq, comparator_15_eq,
       comparator_16_eq, decoder_1_out0, decoder_1_out1, decoder_1_out2, decoder_1_out3, decoder_1_out4,
       decoder_1_out5, decoder_1_out6, decoder_1_out7, decoder_1_out8, decoder_1_out9, decoder_1_out10,
       decoder_1_out11, decoder_1_out12, decoder_1_out13, decoder_1_out14, decoder_1_out15, decoder_2_out0,
       decoder_2_out1, decoder_2_out2, decoder_2_out3, is_add, is_addi, is_jalr, is_lbu, is_lui, is_lw,
       is_RAM_IO, is_sb, is_sw, RAM_BE0, RAM_BE1, RAM_BE2, RAM_BE3, RAM_WE, reset, write_rd;
  wire [1:0] sb_byte_selector;
  wire [2:0] funct3;
  wire [3:0] rd_selector, rs1_selector, rs2_selector;
  wire [4:0] bit_extender_18_out, I_Type_imm, lbu_byte_selector, multiplier_1_out, multiplier_2_out;
  wire [6:0] funct7, opcode;
  wire [19:7] operation;
  wire [23:0] bit_extender_1_out, bit_extender_2_out;
  wire [31:0] adder_1_out, adder_2_out, adder_3_out, adder_4_out, adder_5_out, adder_6_out, adder_7_out,
       adder_8_out, and_1_out, and_2_out, and_10_out, bit_extender_3_out, bit_extender_4_out,
       bit_extender_5_out, bit_extender_14_out, bit_extender_15_out, bit_extender_16_out,
       bit_extender_17_out, new_PC_data, new_RAM_data, PC_data, RAM_data, rs1_data, rs2_data, shifter_1_out,
       shifter_2_out, shifter_3_out, shifter_4_out, shifter_5_out, shifter_6_out, shifter_7_out,
       shifter_8_out, shifter_9_out, shifter_10_out, target_addr, write_data, x0_zero_q, x1_ra_q, x2_sp_q,
       x3_gp_q, x4_tp_q, x5_t0_q, x6_t1_q, x7_t2_q, x8_s0_fp_q, x9_s1_q, x10_a0_q, x11_a1_q, x12_a2_q,
       x13_a3_q, x14_a4_q, x15_a5_q;

  Clock clock_1 (.out(clock_1_out));
  Clock clock_2 (.out(clock_2_out));
  Counter #(.max('hffffffff), .width(32)) PC_counter (
    .clr(reset), .load(is_jalr), .up(1'b1), .clk(clock_1_out), .D(new_PC_data), .Q(PC_data));  // open: count, carry
  // Probe on write_data
  // NoConnect on decoder_1_out0
  Decoder #(.select(4)) decoder_1 (
    .out0(decoder_1_out0), .out1(decoder_1_out1), .out2(decoder_1_out2), .out3(decoder_1_out3),
    .out4(decoder_1_out4), .out5(decoder_1_out5), .out6(decoder_1_out6), .out7(decoder_1_out7),
    .out8(decoder_1_out8), .out9(decoder_1_out9), .out10(decoder_1_out10), .out11(decoder_1_out11),
    .out12(decoder_1_out12), .out13(decoder_1_out13), .out14(decoder_1_out14), .out15(decoder_1_out15),
    .sel(rd_selector), .en(write_rd));
  // Probe on write_data
  Register #(.width(32)) x0_zero (.D(write_data), .en(1'b0), .clk(clock_2_out), .Q(x0_zero_q), .clr(1'b1));
  Register #(.width(32)) x8_s0_fp (.D(write_data), .en(decoder_1_out8), .clk(clock_2_out), .Q(x8_s0_fp_q), .clr(reset));
  Register #(.width(32)) x1_ra (.D(write_data), .en(decoder_1_out1), .clk(clock_2_out), .Q(x1_ra_q), .clr(reset));
  Register #(.width(32)) x9_s1 (.D(write_data), .en(decoder_1_out9), .clk(clock_2_out), .Q(x9_s1_q), .clr(reset));
  or or_1 (is_RAM_IO, is_lw, is_lbu, is_sw, is_sb);
  or or_2 (RAM_WE, is_sw, is_sb);
  Register #(.width(32)) x2_sp (.D(write_data), .en(decoder_1_out2), .clk(clock_2_out), .Q(x2_sp_q), .clr(reset));
  Register #(.width(32)) x10_a0 (.D(write_data), .en(decoder_1_out10), .clk(clock_2_out), .Q(x10_a0_q), .clr(reset));
  or or_3 (write_rd, is_addi, is_jalr, is_add, is_lui, is_lw, is_lbu);
  // Probe on bit_extender_1_out
  Bit_Extender #(.in_width(32), .out_width(24), .\type ("zero")) bit_extender_1 (
    .in(PC_data), .out(bit_extender_1_out));
  ROM #(.addrWidth(24), .dataWidth(32)) rom_1 (
    .addr(bit_extender_1_out), .data({funct7, I_Type_imm, operation[19:15], funct3, operation[11:7], opcode}));
  Register #(.width(32)) x3_gp (.D(write_data), .en(decoder_1_out3), .clk(clock_2_out), .Q(x3_gp_q), .clr(reset));
  Register #(.width(32)) x11_a1 (.D(write_data), .en(decoder_1_out11), .clk(clock_2_out), .Q(x11_a1_q), .clr(reset));
  Register #(.width(32)) x4_tp (.D(write_data), .en(decoder_1_out4), .clk(clock_2_out), .Q(x4_tp_q), .clr(reset));
  Register #(.width(32)) x12_a2 (.D(write_data), .en(decoder_1_out12), .clk(clock_2_out), .Q(x12_a2_q), .clr(reset));
  Register #(.width(32)) x5_t0 (.D(write_data), .en(decoder_1_out5), .clk(clock_2_out), .Q(x5_t0_q), .clr(reset));
  Register #(.width(32)) x13_a3 (.D(write_data), .en(decoder_1_out13), .clk(clock_2_out), .Q(x13_a3_q), .clr(reset));
  Register #(.width(32)) x6_t1 (.D(write_data), .en(decoder_1_out6), .clk(clock_2_out), .Q(x6_t1_q), .clr(reset));
  Register #(.width(32)) x14_a4 (.D(write_data), .en(decoder_1_out14), .clk(clock_2_out), .Q(x14_a4_q), .clr(reset));
  Decoder #(.select(2)) decoder_2 (
    .out0(decoder_2_out0), .out1(decoder_2_out1), .out2(decoder_2_out2), .out3(decoder_2_out3),
    .sel(sb_byte_selector), .en(is_sb));
  // Probe on {funct7, I_Type_imm, operation[19:15], funct3, operation[11:7], opcode}
  Register #(.width(32)) x7_t2 (.D(write_data), .en(decoder_1_out7), .clk(clock_2_out), .Q(x7_t2_q), .clr(reset));
  Register #(.width(32)) x15_a5 (.D(write_data), .en(decoder_1_out15), .clk(clock_2_out), .Q(x15_a5_q), .clr(reset));
  or or_4 (RAM_BE0, is_sw, decoder_2_out0);
  or or_5 (RAM_BE1, is_sw, decoder_2_out1);
  or or_6 (RAM_BE2, is_sw, decoder_2_out2);
  or or_7 (RAM_BE3, is_sw, decoder_2_out3);
  Button reset_button (.out(reset));
  // Probe on target_addr
  Clock clock_3 (.out(clock_3_out));
  // Probe on new_RAM_data
  // Probe on bit_extender_2_out
  Bit_Extender #(.in_width(32), .out_width(24), .\type ("zero")) bit_extender_2 (
    .in(target_addr), .out(bit_extender_2_out));
  RAM #(.addrWidth(24), .asyncread("true"), .byteenables("byteEnables"), .dataWidth(32), .\type ("nonvolatile")) ram_1 (
    .addr(bit_extender_2_out), .we(RAM_WE), .oe(1'b1), .clk(clock_3_out), .din(new_RAM_data),
    .dout(RAM_data), .be3(RAM_BE3), .be2(RAM_BE2), .be1(RAM_BE1), .be0(RAM_BE0));
  Multiplexer #(.select(4), .width(32)) multiplexer_1 (
    .in0(x0_zero_q), .in1(x1_ra_q), .in2(x2_sp_q), .in3(x3_gp_q), .in4(x4_tp_q), .in5(x5_t0_q),
    .in6(x6_t1_q), .in7(x7_t2_q), .in8(x8_s0_fp_q), .in9(x9_s1_q), .in10(x10_a0_q), .in11(x11_a1_q),
    .in12(x12_a2_q), .in13(x13_a3_q), .in14(x14_a4_q), .in15(x15_a5_q), .out(rs1_data), .sel(rs1_selector));
  // Probe on rs2_data
  Multiplexer #(.select(4), .width(32)) multiplexer_2 (
    .in0(x0_zero_q), .in1(x1_ra_q), .in2(x2_sp_q), .in3(x3_gp_q), .in4(x4_tp_q), .in5(x5_t0_q),
    .in6(x6_t1_q), .in7(x7_t2_q), .in8(x8_s0_fp_q), .in9(x9_s1_q), .in10(x10_a0_q), .in11(x11_a1_q),
    .in12(x12_a2_q), .in13(x13_a3_q), .in14(x14_a4_q), .in15(x15_a5_q), .out(rs2_data), .sel(rs2_selector));
  // Probe on rs1_data
  // Probe on RAM_data
  assign bit_extender_3_out = {{20{funct7[6]}}, {funct7, I_Type_imm}};  // Bit_Extender bit_extender_3
  assign bit_extender_4_out = {{20{funct7[6]}}, {funct7, I_Type_imm}};  // Bit_Extender bit_extender_4
  // Probe on adder_1_out
  Adder #(.width(32)) adder_1 (.a(rs1_data), .b(rs2_data), .out(adder_1_out));  // open: cin, cout
  assign bit_extender_5_out = {{12{1'b0}}, {funct7, I_Type_imm, operation[19:15], funct3}};  // Bit_Extender bit_extender_5
  Bit_Extender #(.in_width(5), .out_width(4), .\type ("zero")) bit_extender_6 (.in(operation[11:7]), .out(rd_selector));
  Bit_Extender #(.in_width(5), .out_width(4), .\type ("zero")) bit_extender_7 (
    .in(operation[19:15]), .out(rs1_selector));
  Bit_Extender #(.in_width(5), .out_width(4), .\type ("zero")) bit_extender_8 (.in(operation[11:7]), .out(rd_selector));
  Bit_Extender #(.in_width(5), .out_width(4), .\type ("zero")) bit_extender_9 (
    .in(operation[19:15]), .out(rs1_selector));
  Bit_Extender #(.in_width(5), .out_width(4), .\type ("zero")) bit_extender_10 (.in(I_Type_imm), .out(rs2_selector));
  Bit_Extender #(.in_width(5), .out_width(4), .\type ("zero")) bit_extender_11 (
    .in(operation[11:7]), .out(rd_selector));
  Bit_Extender #(.in_width(5), .out_width(4), .\type ("zero")) bit_extender_12 (
    .in(operation[19:15]), .out(rs1_selector));
  Bit_Extender #(.in_width(5), .out_width(4), .\type ("zero")) bit_extender_13 (.in(I_Type_imm), .out(rs2_selector));
  // Probe on adder_2_out
  Adder #(.width(32)) adder_2 (.a(bit_extender_3_out), .b(rs1_data), .out(adder_2_out));  // open: cin, cout
  Adder #(.width(32)) adder_3 (.a(bit_extender_4_out), .b(rs1_data), .out(adder_3_out));  // open: cin, cout
  assign write_data = is_add ? adder_1_out : 32'bz;  // Controlled_Buffer controlled_buffer_1
  // Probe on shifter_1_out
  Shifter #(.width(32)) shifter_1 (.in(bit_extender_5_out), .\dist (5'b01100), .out(shifter_1_out));
  // Probe on adder_3_out
  Adder #(.width(32)) adder_4 (.a(PC_data), .b(32'h1), .out(adder_4_out));  // open: cin, cout
  assign write_data = is_lui ? shifter_1_out : 32'bz;  // Controlled_Buffer controlled_buffer_2
  assign write_data = is_addi ? adder_2_out : 32'bz;  // Controlled_Buffer controlled_buffer_3
  Shifter #(.shift("lr"), .width(32)) shifter_2 (.in(adder_3_out), .\dist (5'b00010), .out(shifter_2_out));
  Shifter #(.width(32)) shifter_3 (.in(adder_4_out), .\dist (5'b00010), .out(shifter_3_out));
  assign new_PC_data = is_jalr ? shifter_2_out : 32'bz;  // Controlled_Buffer controlled_buffer_4
  assign write_data = is_jalr ? shifter_3_out : 32'bz;  // Controlled_Buffer controlled_buffer_5
  // Probe on opcode
  // Probe on funct3
  // Probe on funct7
  // Probe on rd_selector
  // Probe on rs1_selector
  // Probe on rs2_selector
  // Probe on {funct7, I_Type_imm}
  // Probe on {funct7, I_Type_imm, operation[19:15], funct3}
  // Probe on {funct7, operation[11:7]}
  assign bit_extender_14_out = {{20{funct7[6]}}, {funct7, I_Type_imm}};  // Bit_Extender bit_extender_14
  assign bit_extender_15_out = {{20{funct7[6]}}, {funct7, operation[11:7]}};  // Bit_Extender bit_extender_15
  assign bit_extender_16_out = {{20{funct7[6]}}, {funct7, I_Type_imm}};  // Bit_Extender bit_extender_16
  Multiplier #(.width(5)) multiplier_1 (
    .a(lbu_byte_selector), .b(5'b01000), .out(multiplier_1_out));  // open: cin, cout
  assign bit_extender_17_out = {{20{funct7[6]}}, {funct7, operation[11:7]}};  // Bit_Extender bit_extender_17
  assign bit_extender_18_out = {{3{1'b0}}, sb_byte_selector};  // Bit_Extender bit_extender_18
  Adder #(.width(32)) adder_5 (.a(bit_extender_14_out), .b(rs1_data), .out(adder_5_out));  // open: cin, cout
  Adder #(.width(32)) adder_6 (.a(bit_extender_15_out), .b(rs1_data), .out(adder_6_out));  // open: cin, cout
  assign new_RAM_data = is_sw ? rs2_data : 32'bz;  // Controlled_Buffer controlled_buffer_6
  // Probe on adder_7_out
  Adder #(.width(32)) adder_7 (.a(bit_extender_16_out), .b(rs1_data), .out(adder_7_out));  // open: cin, cout
  // Probe on multiplier_1_out
  // Probe on adder_8_out
  Adder #(.width(32)) adder_8 (.a(bit_extender_17_out), .b(rs1_data), .out(adder_8_out));  // open: cin, cout
  Multiplier #(.width(5)) multiplier_2 (
    .a(bit_extender_18_out), .b(5'b01000), .out(multiplier_2_out));  // open: cin, cout
  Comparator #(.mode("unsigned"), .width(7)) comparator_1 (
    .a(7'b0010011), .b(opcode), .eq(comparator_1_eq));  // open: gt, lt
  Comparator #(.mode("unsigned"), .width(3)) comparator_2 (
    .a(3'b000), .b(funct3), .eq(comparator_2_eq));  // open: gt, lt
  Comparator #(.mode("unsigned"), .width(7)) comparator_3 (
    .a(7'b1100111), .b(opcode), .eq(comparator_3_eq));  // open: gt, lt
  Comparator #(.mode("unsigned"), .width(3)) comparator_4 (
    .a(3'b000), .b(funct3), .eq(comparator_4_eq));  // open: gt, lt
  Comparator #(.mode("unsigned"), .width(7)) comparator_5 (
    .a(7'b0110011), .b(opcode), .eq(comparator_5_eq));  // open: gt, lt
  Comparator #(.mode("unsigned"), .width(3)) comparator_6 (
    .a(3'b000), .b(funct3), .eq(comparator_6_eq));  // open: gt, lt
  Comparator #(.mode("unsigned"), .width(7)) comparator_7 (
    .a({7{1'b0}}), .b(funct7), .eq(comparator_7_eq));  // open: gt, lt
  Comparator #(.mode("unsigned"), .width(7)) comparator_8 (.a(7'b0110111), .b(opcode), .eq(is_lui));  // open: gt, lt
  Comparator #(.mode("unsigned"), .width(7)) comparator_9 (
    .a(7'b0000011), .b(opcode), .eq(comparator_9_eq));  // open: gt, lt
  Comparator #(.mode("unsigned"), .width(3)) comparator_10 (
    .a(3'b010), .b(funct3), .eq(comparator_10_eq));  // open: gt, lt
  Comparator #(.mode("unsigned"), .width(7)) comparator_11 (
    .a(7'b0000011), .b(opcode), .eq(comparator_11_eq));  // open: gt, lt
  Comparator #(.mode("unsigned"), .width(3)) comparator_12 (
    .a(3'b100), .b(funct3), .eq(comparator_12_eq));  // open: gt, lt
  Comparator #(.mode("unsigned"), .width(7)) comparator_13 (
    .a(7'b0100011), .b(opcode), .eq(comparator_13_eq));  // open: gt, lt
  Comparator #(.mode("unsigned"), .width(3)) comparator_14 (
    .a(3'b010), .b(funct3), .eq(comparator_14_eq));  // open: gt, lt
  Comparator #(.mode("unsigned"), .width(7)) comparator_15 (
    .a(7'b0100011), .b(opcode), .eq(comparator_15_eq));  // open: gt, lt
  Comparator #(.mode("unsigned"), .width(3)) comparator_16 (
    .a(3'b000), .b(funct3), .eq(comparator_16_eq));  // open: gt, lt
  // Probe on adder_5_out
  assign write_data = is_lw ? RAM_data : 32'bz;  // Controlled_Buffer controlled_buffer_7
  // Probe on adder_6_out
  Shifter #(.shift("lr"), .width(32)) shifter_4 (.in(adder_6_out), .\dist (5'b00010), .out(shifter_4_out));
  Shifter #(.shift("lr"), .width(32)) shifter_5 (.in(adder_7_out), .\dist (5'b00010), .out(shifter_5_out));
  assign and_1_out = adder_7_out & 32'h3;  // AND_Gate and_1, 32 bits wide
  Shifter #(.width(32)) shifter_6 (.in(32'hff), .\dist (multiplier_1_out), .out(shifter_6_out));
  Shifter #(.shift("lr"), .width(32)) shifter_7 (.in(adder_8_out), .\dist (5'b00010), .out(shifter_7_out));
  assign and_2_out = adder_8_out & 32'h3;  // AND_Gate and_2, 32 bits wide
  and and_3 (is_addi, comparator_1_eq, comparator_2_eq);
  and and_4 (is_jalr, comparator_3_eq, comparator_4_eq);
  and and_5 (is_add, comparator_5_eq, comparator_6_eq, comparator_7_eq);
  and and_6 (is_lw, comparator_9_eq, comparator_10_eq);
  and and_7 (is_lbu, comparator_11_eq, comparator_12_eq);
  and and_8 (is_sw, comparator_13_eq, comparator_14_eq);
  and and_9 (is_sb, comparator_15_eq, comparator_16_eq);
  // Probe on shifter_8_out
  assign target_addr = is_lw ? shifter_8_out : 32'bz;  // Controlled_Buffer controlled_buffer_8
  Shifter #(.shift("lr"), .width(32)) shifter_8 (.in(adder_5_out), .\dist (5'b00010), .out(shifter_8_out));
  // Probe on shifter_4_out
  assign target_addr = is_sw ? shifter_4_out : 32'bz;  // Controlled_Buffer controlled_buffer_9
  // Probe on shifter_5_out
  assign target_addr = is_lbu ? shifter_5_out : 32'bz;  // Controlled_Buffer controlled_buffer_10
  Bit_Extender #(.in_width(32), .out_width(5), .\type ("zero")) bit_extender_19 (
    .in(and_1_out), .out(lbu_byte_selector));
  assign and_10_out = RAM_data & shifter_6_out;  // AND_Gate and_10, 32 bits wide
  // Probe on shifter_7_out
  assign target_addr = is_sb ? shifter_7_out : 32'bz;  // Controlled_Buffer controlled_buffer_11
  Bit_Extender #(.in_width(32), .out_width(2), .\type ("zero")) bit_extender_20 (
    .in(and_2_out), .out(sb_byte_selector));
  Shifter #(.width(32)) shifter_9 (.in(rs2_data), .\dist (multiplier_2_out), .out(shifter_9_out));
  Shifter #(.shift("lr"), .width(32)) shifter_10 (.in(and_10_out), .\dist (multiplier_1_out), .out(shifter_10_out));
  assign new_RAM_data = is_sb ? shifter_9_out : 32'bz;  // Controlled_Buffer controlled_buffer_12
  // Probe on lbu_byte_selector
  // Probe on shifter_10_out
  assign write_data = is_lbu ? shifter_10_out : 32'bz;  // Controlled_Buffer controlled_buffer_13

  // Other names for the same wires on the sheet: operation (some bits) = {funct7, I_Type_imm, funct3, opcode};
  //   U_Type_imm[19:0] = {funct7, I_Type_imm, operation[19:15], funct3}; S_Type_imm[11:0] = {funct7, operation[11:7]};
  //   I_Type_imm[11:5] = funct7; write_PC = is_jalr

  // Notes on the sheet:
  //   contents of rom_1 (hex, n*v repeats v):
  //   413 52137 10113 10b7 22408093 80e7 fea12823 fe812e23 1437 40840413 ff014183 3401b3 1c183 ff114203
  //   440233 24203 4181b3 ff214203 440233 24203 4181b3 ff314203 440233 24203 4181b3 1237 40020213 320233
  //   24203 ffc12403 420233 420233 410233 a000193 fe312823 9c00193 fe312623 fec22203 20067 8067 ff410113
  //   100513 112423 10b7 21808093 80e7 fec10113 912423 494b7 6b048493 812623 112823 496b7 69068693 48413
  //   48713 fe012823 174183 fe3109a3 ff012183 fe812e23 fe312823 3d437 60040413 ff214203 420233 420233
  //   440233 22203 fe412623 ff114203 420233 420233 440233 22203 fe412423 ff014203 420233 420233 440233
  //   22203 fe412223 fed14183 fea14203 4181b3 fe714203 4181b3 fe312223 fee14183 feb14203 4181b3 fe3102a3
  //   fef14183 fe310323 fe412183 8237 20213 440433 ff314203 420233 420233 440233 22203 ffc12403 4181b3
  //   74503 350533 6a603 270713 468693 fe312a23 fec12423 31237 50020213 feb14183 4181b3 1c183 fe3103a3
  //   fea14183 4181b3 1c183 fe310323 fe914183 4181b3 1c183 fe3102a3 fe814183 4181b3 1c183 fe310223
  //   ff412183 fe412203 450533 150513 fea12823 fe812e23 1437 40840413 ff014183 3401b3 1c183 ff114203
  //   440233 24203 4181b3 ff214203 440233 24203 4181b3 ff314203 440233 24203 4181b3 1237 40020213 320233
  //   24503 ffc12403 e12223 d12023 1800093 80e7 412703 497b7 6c078793 12683 fee12823 fef12623 fe812e23
  //   fe912c23 1437 30040413 ff014183 340233 100193 320023 fec14183 3401b3 18023 24183 ff114483 940233
  //   100493 920023 fed14483 9404b3 48023 24483 9181b3 ff214483 940233 100493 920023 fee14483 9404b3 48023
  //   24483 9181b3 ff314483 940233 100493 920023 fef14483 9404b3 48023 24483 9181b3 1237 40020213 320233
  //   24203 ff812483 ffc12403 420233 420233 410233 37800193 fe312823 e000193 fe312623 fec22203 20067 49737
  //   67070713 72683 fe012823 14c203 fe4108a3 ff012203 4c503 450533 470713 e12023 fe312a23 fed12423 31237
  //   50020213 feb14183 4181b3 1c183 fe3103a3 fea14183 4181b3 1c183 fe310323 fe914183 4181b3 1c183
  //   fe3102a3 fe814183 4181b3 1c183 fe310223 ff412183 fe412203 450533 150513 fea12823 fe812e23 1437
  //   40840413 ff014183 3401b3 1c183 ff114203 440233 24203 4181b3 ff214203 440233 24203 4181b3 ff314203
  //   440233 24203 4181b3 1237 40020213 320233 24503 ffc12403 1800093 80e7 248493 497b7 6c078793 12703
  //   fe912823 fef12623 fe812e23 fe912c23 1437 30040413 ff014183 340233 100193 320023 fec14183 3401b3
  //   18023 24183 ff114483 940233 100493 920023 fed14483 9404b3 48023 24483 9181b3 ff214483 940233 100493
  //   920023 fee14483 9404b3 48023 24483 9181b3 ff314483 940233 100493 920023 fef14483 9404b3 48023 24483
  //   9181b3 1237 40020213 320233 24203 ff812483 ffc12403 420233 420233 410233 55c00193 fe312823 38000193
  //   fe312623 fec22203 20067 244683 144603 344703 444783 494b7 64048493 8*d686b3 fed12823 fec12623 116b7
  //   60068693 fe012223 ff314203 fe4102a3 fef14203 fe410223 fe412203 468233 24203 fe4105a3 ff214203
  //   fe4102a3 fee14203 fe410223 fe412203 468233 24203 fe410523 ff114203 fe4102a3 fed14203 fe410223
  //   fe412203 468233 24203 fe4104a3 ff014203 fe4102a3 fec14203 fe410223 fe412203 468233 24203 fe410423
  //   fe812683 4a503 fe012823 fee10923 fee12423 fe914203 fe4109a3 ff012703 fee12823 fed12623 11737
  //   60070713 fe012223 ff314203 fe4102a3 fef14203 fe410223 fe412203 470233 24203 fe4105a3 ff214203
  //   fe4102a3 fee14203 fe410223 fe412203 470233 24203 fe410523 ff114203 fe4102a3 fed14203 fe410223
  //   fe412203 470233 24203 fe4104a3 ff014203 fe4102a3 fec14203 fe410223 fe412203 470233 24203 fe410423
  //   fe812703 fe012823 fef109a3 ff012783 fef12823 fee12623 117b7 60078793 fe012223 ff314203 fe4102a3
  //   fef14203 fe410223 fe412203 478233 24203 fe4105a3 ff214203 fe4102a3 fee14203 fe410223 fe412203 478233
  //   24203 fe410523 ff114203 fe4102a3 fed14203 fe410223 fe412203 478233 24203 fe4104a3 ff014203 fe4102a3
  //   fec14203 fe410223 fe412203 478233 24203 fe410423 fe812783 fe312a23 fef12423 31237 50020213 feb14183
  //   4181b3 1c183 fe3103a3 fea14183 4181b3 1c183 fe310323 fe914183 4181b3 1c183 fe3102a3 fe814183 4181b3
  //   1c183 fe310223 ff412183 fe412203 450533 150513 fea12823 fe812e23 1437 40840413 ff014183 3401b3 1c183
  //   ff114203 440233 24203 4181b3 ff214203 440233 24203 4181b3 ff314203 440233 24203 4181b3 1237 400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
  //   I-Type Parse
  //   R-Type Parse
  //   U-Type Parse
  //   S-Type Parse
  //   ADDI
  //   JALR
  //   ADD
  //   LUI
  //   Operation Parser
  //   rd 中存储 PC+1
  //   Operation Options
  //   LW
  //   SW
  //   LBU
  //   SB
  //   Operation Judement
endmodule
